# Fritzing sketch Mainboard (saved by Fritzing 0.9.4)
circuit board: 10.22cm x 7cm
breadboards: 1

parts:
  R7 = Resistor [tolerance=±5% resistance=1k package=THT]
  R8 = Resistor [tolerance=±5% resistance=10k package=THT]
  R9 = Resistor [tolerance=±5% resistance=1k package=THT]
  R10 = Resistor [tolerance=±5% resistance=10k package=THT]
  R11 = Resistor [tolerance=±5% resistance=1k package=THT]
  R12 = Resistor [tolerance=±5% resistance=10k package=THT]
  Q4 = TIP120 Hi-Current Darlington Transistor
  Q5 = TIP120 Hi-Current Darlington Transistor
  Q6 = TIP120 Hi-Current Darlington Transistor
  ON/OFF = male pin header, 2 pins [form="♂ (male)"]
  Power = male pin header, 2 pins [form="♂ (male)"]
  LED_Strip = male pin header, 4 pins [form="♂ (male)"]
  Voltage_regulator = Voltage Regulator - 5V [package="TO220 [THT]"]
  Positive_terminal = male pin header, 13 pins [form="♂ (male)"]
  Negative_terminal = male pin header, 13 pins [form="♂ (male)"]
  MH-ET_Live_Minikit_for_ESP1 = MH-ET Live Minikit for ESP32

nets:
  N1: R7.Pin_0, R8.Pin_1, Q4.BASE
  N2: R7.Pin_1, MH-ET_Live_Minikit_for_ESP1.TDO
  GND: R8.Pin_0, R10.Pin_0, R12.Pin_0, Q4.EMITTER, Q5.EMITTER, Q6.EMITTER, Power.pin1, Voltage_regulator.GND, Negative_terminal.pin1, Negative_terminal.pin2, Negative_terminal.pin3, Negative_terminal.pin4, Negative_terminal.pin5, Negative_terminal.pin6, Negative_terminal.pin7, Negative_terminal.pin8, Negative_terminal.pin9, Negative_terminal.pin10, Negative_terminal.pin11, Negative_terminal.pin12, Negative_terminal.pin13, MH-ET_Live_Minikit_for_ESP1.GND
  N3: R9.Pin_0, R10.Pin_1, Q5.BASE
  N4: R9.Pin_1, MH-ET_Live_Minikit_for_ESP1.IO16
  N5: R11.Pin_0, R12.Pin_1, Q6.BASE
  N6: R11.Pin_1, MH-ET_Live_Minikit_for_ESP1.IO17
  N7: Q4.COLLECTOR, LED_Strip.pin3
  N8: Q5.COLLECTOR, LED_Strip.pin2
  N9: Q6.COLLECTOR, LED_Strip.pin1
  N10: ON/OFF.pin1, LED_Strip.pin4, Voltage_regulator.input_voltage
  N11: ON/OFF.pin2, Power.pin2
  N12: Voltage_regulator.output_voltage, Positive_terminal.pin1, Positive_terminal.pin2, Positive_terminal.pin3, Positive_terminal.pin4, Positive_terminal.pin5, Positive_terminal.pin6, Positive_terminal.pin7, Positive_terminal.pin8, Positive_terminal.pin9, Positive_terminal.pin10, Positive_terminal.pin11, Positive_terminal.pin12, Positive_terminal.pin13, MH-ET_Live_Minikit_for_ESP1.VCC

custom parts:
  MH-ET Live Minikit for ESP32: MH-ET Live Minikit for ESP32 ( http://mh.nodebb.com/topic/8/mh-et-live-minikit-for-esp32/2/) PCB footprint is invalid.
