# Fritzing sketch Menu buttons (saved by Fritzing 0.9.4)
circuit board: 10.22cm x 1.6cm
breadboards: 1

parts:
  B2 = Pushbutton [package="[THT]"]
  B3 = Pushbutton [package="[THT]"]
  Mainboard = male pin header, 3 pins [form="♂ (male)"]

nets:
  N1: B2.Pin_1, B2.Pin_2, Mainboard.pin3
  N2: B2.Pin_3, B2.Pin_4, B3.Pin_3, B3.Pin_4, Mainboard.pin1
  N3: B3.Pin_1, B3.Pin_2, Mainboard.pin2
